// Logisim project projeto3.circ as structural Verilog: 5 circuits, main circuit main
module main (
);

  wire Clock, RegWrite, RESET, WBSel;
  wire [2:0] ALUop, Funct3;
  wire [3:0] Opcode;
  wire [7:0] instructor_fetch_1_pc;
  wire [12:4] rom_1_data;
  wire [15:0] alu_1_alures, Immed16, multiplexer_1_out, register_file_1_out_rd, register_file_1_out_rs1,
       register_file_1_out_rs1_next, register_file_1_out_rs2, register_file_1_out_rs2_next;

  Clock clock_1 (.out(Clock));
  Button button_1 (.out(RESET));
  ROM #(.dataWidth(16)) rom_1 (.addr(instructor_fetch_1_pc), .data({Funct3, rom_1_data, Opcode}));
  INSTRUCTOR_FETCH instructor_fetch_1 (.CLK(Clock), .RESET(RESET), .PC(instructor_fetch_1_pc));
  assign Immed16 = {{7{Funct3[2]}}, {Funct3, rom_1_data[12:7]}};  // Bit_Extender bit_extender_1
  CONTROL_UNIT control_unit_1 (.Opcode(Opcode), .Funct3(Funct3), .ALUop(ALUop), .RegWrite(RegWrite), .WBSel(WBSel));
  REGISTER_FILE register_file_1 (
    .Clk(Clock), .RegWrite(RegWrite), .WriteData(multiplexer_1_out), .WriteAddr(rom_1_data[6:4]),
    .ReadAddr_rd(rom_1_data[6:4]), .ReadAddr_rs1(rom_1_data[9:7]), .ReadAddr_rs2(rom_1_data[12:10]),
    .RESET(RESET), .Out_Rd(register_file_1_out_rd), .Out_Rs1(register_file_1_out_rs1),
    .Out_Rs2(register_file_1_out_rs2), .Out_Rs1_next(register_file_1_out_rs1_next),
    .Out_Rs2_next(register_file_1_out_rs2_next));
  ALU alu_1 (
    .In_Rd(register_file_1_out_rd), .In_Rs1(register_file_1_out_rs1), .In_Rs2(register_file_1_out_rs2),
    .In_Rs1_next(register_file_1_out_rs1_next), .In_Rs2_next(register_file_1_out_rs2_next), .ALUOp(ALUop),
    .ALURes(alu_1_alures));
  Multiplexer #(.width(16)) multiplexer_1 (.in0(alu_1_alures), .in1(Immed16), .out(multiplexer_1_out), .sel(WBSel));

  // Notes on the sheet:
  //   contents of rom_1 (hex, n*v repeats v):
  //   101 191 221 131 c1 2d1 161 171 5b8 4808 3a08
  //   Immed9
  //   Rd
  //   Rs1
  //   Rs2
  //   WriteData
  //   Rd
  //   Rs1
  //   Rs2
  //   Rs1+1
  //   Rs2+1
  //   ALURes
endmodule

module REGISTER_FILE (
  input  Clk,
  input  RegWrite,
  input  [15:0] WriteData,
  input  [2:0] WriteAddr,
  input  [2:0] ReadAddr_rd,
  input  [2:0] ReadAddr_rs1,
  input  [2:0] ReadAddr_rs2,
  input  RESET,
  output [15:0] Out_Rd,
  output [15:0] Out_Rs1,
  output [15:0] Out_Rs2,
  output [15:0] Out_Rs1_next,
  output [15:0] Out_Rs2_next
);

  wire WE_R0, WE_R1, WE_R2, WE_R3, WE_R4, WE_R5, WE_R6, WE_R7;
  wire [2:0] Addr_rs1_next, Addr_rs2_next;
  wire [15:0] RData_R0, RData_R1, RData_R2, RData_R3, RData_R4, RData_R5, RData_R6, RData_R7;

  Decoder #(.select(3)) decoder_1 (
    .out0(WE_R0), .out1(WE_R1), .out2(WE_R2), .out3(WE_R3), .out4(WE_R4), .out5(WE_R5), .out6(WE_R6),
    .out7(WE_R7), .sel(WriteAddr), .en(RegWrite));
  Adder #(.width(3)) adder_1 (.a(3'b000), .b(ReadAddr_rs1), .out(Addr_rs1_next), .cin(1'b1));  // open: cout
  Adder #(.width(3)) adder_2 (.a(3'b000), .b(ReadAddr_rs2), .out(Addr_rs2_next), .cin(1'b1));  // open: cout
  Register #(.width(16)) R0 (.D(WriteData), .en(WE_R0), .clk(Clk), .Q(RData_R0), .clr(RESET));
  Register #(.width(16)) R2 (.D(WriteData), .en(WE_R2), .clk(Clk), .Q(RData_R2), .clr(RESET));
  Register #(.width(16)) R4 (.D(WriteData), .en(WE_R4), .clk(Clk), .Q(RData_R4), .clr(RESET));
  Register #(.width(16)) R6 (.D(WriteData), .en(WE_R6), .clk(Clk), .Q(RData_R6), .clr(RESET));
  Register #(.width(16)) R1 (.D(WriteData), .en(WE_R1), .clk(Clk), .Q(RData_R1), .clr(RESET));
  Register #(.width(16)) R3 (.D(WriteData), .en(WE_R3), .clk(Clk), .Q(RData_R3), .clr(RESET));
  Register #(.width(16)) R5 (.D(WriteData), .en(WE_R5), .clk(Clk), .Q(RData_R5), .clr(RESET));
  Register #(.width(16)) R7 (.D(WriteData), .en(WE_R7), .clk(Clk), .Q(RData_R7), .clr(RESET));
  Multiplexer #(.select(3), .width(16)) multiplexer_1 (
    .in0(RData_R0), .in1(RData_R1), .in2(RData_R2), .in3(RData_R3), .in4(RData_R4), .in5(RData_R5),
    .in6(RData_R6), .in7(RData_R7), .out(Out_Rd), .sel(ReadAddr_rd));
  Multiplexer #(.select(3), .width(16)) multiplexer_2 (
    .in0(RData_R0), .in1(RData_R1), .in2(RData_R2), .in3(RData_R3), .in4(RData_R4), .in5(RData_R5),
    .in6(RData_R6), .in7(RData_R7), .out(Out_Rs1), .sel(ReadAddr_rs1));
  Multiplexer #(.select(3), .width(16)) multiplexer_3 (
    .in0(RData_R0), .in1(RData_R1), .in2(RData_R2), .in3(RData_R3), .in4(RData_R4), .in5(RData_R5),
    .in6(RData_R6), .in7(RData_R7), .out(Out_Rs2), .sel(ReadAddr_rs2));
  Multiplexer #(.select(3), .width(16)) multiplexer_4 (
    .in0(RData_R0), .in1(RData_R1), .in2(RData_R2), .in3(RData_R3), .in4(RData_R4), .in5(RData_R5),
    .in6(RData_R6), .in7(RData_R7), .out(Out_Rs1_next), .sel(Addr_rs1_next));
  Multiplexer #(.select(3), .width(16)) multiplexer_5 (
    .in0(RData_R0), .in1(RData_R1), .in2(RData_R2), .in3(RData_R3), .in4(RData_R4), .in5(RData_R5),
    .in6(RData_R6), .in7(RData_R7), .out(Out_Rs2_next), .sel(Addr_rs2_next));

  // Other names for the same wires on the sheet: Addr_rd[2:0] = ReadAddr_rd; Addr_rs1[2:0] = ReadAddr_rs1;
  //   Addr_rs2[2:0] = ReadAddr_rs2; RW = RegWrite; WData[15:0] = WriteData
endmodule

module INSTRUCTOR_FETCH (
  input  CLK,
  input  RESET,
  output [7:0] PC
);

  wire [7:0] adder_1_out;

  Register register_1 (.D(adder_1_out), .en(1'b1), .clk(CLK), .Q(PC), .clr(RESET));
  Adder adder_1 (.a(PC), .b({8{1'b0}}), .out(adder_1_out), .cin(1'b1));  // open: cout
endmodule

module ALU (
  input  [15:0] In_Rd,
  input  [15:0] In_Rs1,
  input  [15:0] In_Rs2,
  input  [15:0] In_Rs1_next,
  input  [15:0] In_Rs2_next,
  input  [2:0] ALUOp,
  output [15:0] ALURes
);

  wire [15:0] multiplier_1_out, multiplier_2_out, RES_ADD, RES_DOT, RES_DOTA;

  Adder #(.width(16)) adder_1 (.a(In_Rs1), .b(In_Rs2), .out(RES_ADD));  // open: cin, cout
  Multiplier #(.width(16)) multiplier_1 (.a(In_Rs1), .b(In_Rs2), .out(multiplier_1_out));  // open: cin, cout
  Adder #(.width(16)) adder_2 (.a(multiplier_1_out), .b(multiplier_2_out), .out(RES_DOT));  // open: cin, cout
  Multiplier #(.width(16)) multiplier_2 (.a(In_Rs1_next), .b(In_Rs2_next), .out(multiplier_2_out));  // open: cin, cout
  Adder #(.width(16)) adder_3 (.a(RES_DOT), .b(In_Rd), .out(RES_DOTA));  // open: cin, cout
  Multiplexer #(.select(3), .width(16)) multiplexer_1 (
    .in0(RES_ADD), .in1(RES_DOTA), .in2(RES_DOT), .out(ALURes), .sel(ALUOp));  // open: in3, in4, in5, in6, in7

  // Other names for the same wires on the sheet: Op[2:0] = ALUOp; Rd_Data[15:0] = In_Rd; Rs1_Data[15:0] = In_Rs1;
  //   Rs1_Next_Data[15:0] = In_Rs1_next; Rs2_Data[15:0] = In_Rs2; Rs2_Next_Data[15:0] = In_Rs2_next
endmodule

module CONTROL_UNIT (
  input  [3:0] Opcode,
  input  [2:0] Funct3,
  output [2:0] ALUop,
  output RegWrite,
  output WBSel
);

  wire is_Alu, is_Li;

  Comparator #(.width(4)) comparator_1 (.a(4'b0001), .b(Opcode), .eq(is_Li));  // open: gt, lt
  Comparator #(.width(4)) comparator_2 (.a(4'b1000), .b(Opcode), .eq(is_Alu));  // open: gt, lt
  or or_1 (RegWrite, is_Li, is_Alu);
  buf or_2 (WBSel, is_Li);  // OR_Gate

  assign ALUop = Funct3;

  // Other names for the same wires on the sheet: bits3Funct3[2:0] = Funct3; bits4Opcode[3:0] = Opcode

  // Notes on the sheet:
  //   Li
  //   AluOperation
endmodule
